// Logisim project CPU Project.circ as structural Verilog
module reg_16 (
  input  INR,
  input  CLR,
  input  [15:0] Inp,
  input  CLK,
  input  LD,
  output [15:0] Outp
);

  wire [15:0] adder_1_out, multiplexer_1_out, multiplexer_2_out, multiplexer_3_out;

  Adder #(.width(16)) adder_1 (.a(Outp), .b({16{1'b0}}), .out(adder_1_out), .cin(1'b1));  // open: cout
  Multiplexer #(.width(16)) multiplexer_1 (.in0(Outp), .in1(adder_1_out), .out(multiplexer_1_out), .sel(INR));
  Multiplexer #(.width(16)) multiplexer_2 (
    .in0(multiplexer_1_out), .in1({16{1'b0}}), .out(multiplexer_2_out), .sel(CLR));
  Multiplexer #(.width(16)) multiplexer_3 (.in0(multiplexer_2_out), .in1(Inp), .out(multiplexer_3_out), .sel(LD));
  Register #(.width(16)) register_1 (.D(multiplexer_3_out), .clk(CLK), .Q(Outp));  // open: en, clr

  // Other names for the same wires on the sheet: OP[15:0] = Outp
endmodule

module reg_12 (
  input  INR,
  input  CLR,
  input  [15:0] Inp,
  input  CLK,
  input  LD,
  output [11:0] Outp12,
  output [15:0] Outp16
);

  wire [15:0] adder_1_out, multiplexer_1_out, multiplexer_2_out, multiplexer_3_out;

  Adder #(.width(16)) adder_1 (
    .a({Outp16[15:12], Outp12}), .b({16{1'b0}}), .out(adder_1_out), .cin(1'b1));  // open: cout
  Multiplexer #(.width(16)) multiplexer_1 (
    .in0({Outp16[15:12], Outp12}), .in1(adder_1_out), .out(multiplexer_1_out), .sel(INR));
  Multiplexer #(.width(16)) multiplexer_2 (
    .in0(multiplexer_1_out), .in1({16{1'b0}}), .out(multiplexer_2_out), .sel(CLR));
  Multiplexer #(.width(16)) multiplexer_3 (.in0(multiplexer_2_out), .in1(Inp), .out(multiplexer_3_out), .sel(LD));
  Register #(.width(16)) register_1 (.D(multiplexer_3_out), .clk(CLK), .Q({Outp16[15:12], Outp12}));  // open: en, clr

  assign Outp16[11:0] = Outp12;

  // Other names for the same wires on the sheet: OP[15:0] = {Outp16[15:12], Outp12}
endmodule

module sequence_counter (
  input  INR,
  input  CLR,
  input  CLK,
  input  D_ENABLE,
  output [15:0] OUTP
);

  wire [3:0] adder_1_out, multiplexer_1_out, multiplexer_2_out, register_1_q;

  Adder #(.width(4)) adder_1 (.a(register_1_q), .b(4'b0001), .out(adder_1_out));  // open: cin, cout
  Multiplexer #(.width(4)) multiplexer_1 (.in0(register_1_q), .in1(adder_1_out), .out(multiplexer_1_out), .sel(INR));
  Multiplexer #(.width(4)) multiplexer_2 (.in0(multiplexer_1_out), .in1(4'b0000), .out(multiplexer_2_out), .sel(CLR));
  Register #(.width(4)) register_1 (.D(multiplexer_2_out), .clk(CLK), .Q(register_1_q));  // open: en, clr
  Decoder #(.select(4)) decoder_1 (
    .out0(OUTP[0]), .out1(OUTP[1]), .out2(OUTP[2]), .out3(OUTP[3]), .out4(OUTP[4]), .out5(OUTP[5]),
    .out6(OUTP[6]), .out7(OUTP[7]), .out8(OUTP[8]), .out9(OUTP[9]), .out10(OUTP[10]), .out11(OUTP[11]),
    .out12(OUTP[12]), .out13(OUTP[13]), .out14(OUTP[14]), .out15(OUTP[15]), .sel(register_1_q), .en(D_ENABLE));
endmodule

module Data_path (
  input  CLK,
  input  AR_INR,
  input  AR_CLR,
  input  [2:0] BUS_SELECT,
  input  AR_LD,
  input  PC_INR,
  input  PC_CLR,
  input  PC_LD,
  input  DR_INR,
  input  DR_CLR,
  input  DR_LD,
  input  AC_INR,
  input  AC_CLR,
  input  AC_LD,
  input  Cin,
  input  [2:0] ALU_SELECT,
  input  E_COMP,
  input  E_CLR,
  input  E_LD,
  input  IR_LD,
  input  MEMORY_WRITE_ENABLE,
  input  MEMORY_OUT_ENABLE,
  input  rB6,
  input  rB7,
  input  ADD,
  output [15:0] PCout,
  output [15:0] DRout,
  output [15:0] ACout,
  output Eout,
  output [15:0] IRout
);

  wire AC0, AC15, Cout, Einp, multiplexer_1_out, multiplexer_2_out;
  wire [11:0] ADDRESS;
  wire [15:0] alu_1_alu_out, AR_outp16, DATAPATH_OUTPUT, ram_1_dout, TR_outp;

  Multiplexer multiplexer_1 (.in0(Eout), .in1(AC15), .out(multiplexer_1_out), .sel(rB6));
  Multiplexer multiplexer_2 (.in0(multiplexer_1_out), .in1(AC0), .out(multiplexer_2_out), .sel(rB7));
  Multiplexer multiplexer_3 (.in0(multiplexer_2_out), .in1(Cout), .out(Einp), .sel(ADD));
  RAM #(.addrWidth(12), .asyncread("true"), .dataWidth(16)) ram_1 (
    .addr(ADDRESS), .we(MEMORY_WRITE_ENABLE), .oe(MEMORY_OUT_ENABLE), .clk(CLK), .din(DATAPATH_OUTPUT),
    .dout(ram_1_dout));
  reg_12 AR (
    .INR(AR_INR), .CLR(AR_CLR), .Inp(DATAPATH_OUTPUT), .CLK(CLK), .LD(AR_LD), .Outp12(ADDRESS),
    .Outp16(AR_outp16));
  reg_12 PC (.INR(PC_INR), .CLR(PC_CLR), .Inp(DATAPATH_OUTPUT), .CLK(CLK), .LD(PC_LD), .Outp16(PCout));  // open: Outp12
  reg_16 DR (.INR(DR_INR), .CLR(DR_CLR), .Inp(DATAPATH_OUTPUT), .CLK(CLK), .LD(DR_LD), .Outp(DRout));
  reg_16 AC (.INR(AC_INR), .CLR(AC_CLR), .Inp(alu_1_alu_out), .CLK(CLK), .LD(AC_LD), .Outp(ACout));
  ALU alu_1 (
    .Cin(Cin), .AC(ACout), .DR(DRout), .Inp(DATAPATH_OUTPUT), .ALU_SELECT(ALU_SELECT), .SR(Eout), .SL(Eout),
    .ALU_OUT(alu_1_alu_out), .AC0(AC0), .Cout(Cout), .AC15(AC15));
  reg_16 TR (.Inp(DATAPATH_OUTPUT), .CLK(CLK), .Outp(TR_outp));  // open: INR, CLR, LD
  reg_16A IR (.CLK(CLK), .Inp(DATAPATH_OUTPUT), .LD(IR_LD), .Outp(IRout));
  Multiplexer #(.select(3), .width(16)) multiplexer_4 (
    .in1(AR_outp16), .in2(PCout), .in3(DRout), .in4(ACout), .in5(TR_outp), .in6(IRout), .in7(ram_1_dout),
    .out(DATAPATH_OUTPUT), .sel(BUS_SELECT));  // open: in0
  FF E (.Inp(Einp), .CLK(CLK), .E_complement(E_COMP), .CLR(E_CLR), .LD(E_LD), .Op(Eout));

  // Other names for the same wires on the sheet: AC1[15:0] = ACout; CP = CLK; DR1[15:0] = DRout; Eoutp = Eout
endmodule

module control_unit (
  input  SC_INR,
  input  SC_CLR,
  input  CLk,
  input  DECODEENABLE,
  input  [15:0] IR_OUT,
  input  CONTROL,
  output T0,
  output T1,
  output T2,
  output T3,
  output T4,
  output T5,
  output T6,
  output T7,
  output rB0,
  output rB1,
  output rB2,
  output rB3,
  output rB4,
  output rB5,
  output rB6,
  output rB7,
  output rB8,
  output rB9,
  output rB10,
  output rB11,
  output r,
  output B0,
  output B1,
  output B2,
  output B3,
  output B4,
  output B5,
  output B6,
  output B7,
  output B8,
  output B9,
  output B10,
  output B11,
  output D0,
  output D1,
  output D2,
  output D3,
  output D4,
  output D5,
  output D6,
  output D7,
  output I
);

  wire multiplexer_1_out, not_1_out;
  wire [15:8] sequence_counter_1_outp;

  sequence_counter sequence_counter_1 (
    .INR(SC_INR), .CLR(SC_CLR), .CLK(CLk), .D_ENABLE(DECODEENABLE),
    .OUTP({sequence_counter_1_outp, T7, T6, T5, T4, T3, T2, T1, T0}));
  not not_1 (not_1_out, I);
  and and_1 (r, D7, not_1_out, T3);
  Decoder #(.select(3)) decoder_1 (
    .out0(D0), .out1(D1), .out2(D2), .out3(D3), .out4(D4), .out5(D5), .out6(D6), .out7(D7),
    .sel(IR_OUT[14:12]), .en(DECODEENABLE));
  D_Flip_Flop d_ff_1 (.D(multiplexer_1_out), .clk(CLk), .Q(I));  // open: Qn, preset, reset
  Multiplexer multiplexer_1 (.in0(I), .in1(IR_OUT[15]), .out(multiplexer_1_out), .sel(CONTROL));
  and and_2 (rB0, r, IR_OUT[0]);
  and and_3 (rB1, r, IR_OUT[1]);
  and and_4 (rB2, r, IR_OUT[2]);
  and and_5 (rB3, r, IR_OUT[3]);
  and and_6 (rB4, r, IR_OUT[4]);
  and and_7 (rB5, r, IR_OUT[5]);
  and and_8 (rB6, r, IR_OUT[6]);
  and and_9 (rB7, r, IR_OUT[7]);
  and and_10 (rB8, r, IR_OUT[8]);
  and and_11 (rB9, r, IR_OUT[9]);
  and and_12 (rB10, r, IR_OUT[10]);
  and and_13 (rB11, r, IR_OUT[11]);

  assign B0 = IR_OUT[0];
  assign B1 = IR_OUT[1];
  assign B2 = IR_OUT[2];
  assign B3 = IR_OUT[3];
  assign B4 = IR_OUT[4];
  assign B5 = IR_OUT[5];
  assign B6 = IR_OUT[6];
  assign B7 = IR_OUT[7];
  assign B8 = IR_OUT[8];
  assign B9 = IR_OUT[9];
  assign B10 = IR_OUT[10];
  assign B11 = IR_OUT[11];

  // Other names for the same wires on the sheet: CP = CLk; DECODE_ENABLE = DECODEENABLE
endmodule

module ALU (
  input  Cin,
  input  [15:0] AC,
  input  [15:0] DR,
  input  [15:0] Inp,
  input  [2:0] ALU_SELECT,
  input  SR,
  input  SL,
  output [15:0] ALU_OUT,
  output AC0,
  output Cout,
  output AC15
);

  wire [15:0] adder_1_out, and_1_out, not_1_out;

  Adder #(.width(16)) adder_1 (.a(AC), .b(DR), .out(adder_1_out), .cin(Cin), .cout(Cout));
  assign not_1_out = ~AC;  // NOT_Gate not_1, 16 bits wide
  assign and_1_out = AC & DR;  // AND_Gate and_1, 16 bits wide
  Multiplexer #(.select(3), .width(16)) multiplexer_1 (
    .in1(and_1_out), .in2(adder_1_out), .in3(DR), .in4(Inp), .in5(not_1_out), .in6({SR, AC[15:1]}),
    .in7({AC[14:0], SL}), .out(ALU_OUT), .sel(ALU_SELECT));  // open: in0

  assign AC0 = AC[0];
  assign AC15 = AC[15];

  // Other names for the same wires on the sheet: SEL[2:0] = ALU_SELECT
endmodule

module FF (
  input  Inp,
  input  CLK,
  input  E_complement,
  input  CLR,
  input  LD,
  output Op
);

  wire multiplexer_1_out, multiplexer_2_out, multiplexer_3_out, not_1_out;

  not not_1 (not_1_out, Op);
  Multiplexer multiplexer_1 (.in0(Op), .in1(not_1_out), .out(multiplexer_1_out), .sel(E_complement));
  Multiplexer multiplexer_2 (.in0(multiplexer_1_out), .in1(Inp), .out(multiplexer_2_out), .sel(LD));
  Multiplexer multiplexer_3 (.in0(multiplexer_2_out), .in1(1'b0), .out(multiplexer_3_out), .sel(CLR));
  D_Flip_Flop d_ff_1 (.D(multiplexer_3_out), .clk(CLK), .Q(Op));  // open: Qn, preset, reset
endmodule

module reg_16A (
  input  CLK,
  input  [15:0] Inp,
  input  LD,
  output [15:0] Outp
);

  wire [15:0] multiplexer_1_out;

  Multiplexer #(.width(16)) multiplexer_1 (.in0(Outp), .in1(Inp), .out(multiplexer_1_out), .sel(LD));
  Register #(.width(16)) register_1 (.D(multiplexer_1_out), .clk(CLK), .Q(Outp));  // open: en, clr
endmodule

module CPU (
  input  Start,
  output [15:0] DROUT,
  output [15:0] ACOUT,
  output [15:0] IROUT
);

  wire A1, A2, A3, A4, A6, A7, AC_0BIT, AC_CLR, AC_INR, AC_LD, ADDop, and_1_out, and_5_out, and_6_out,
       and_7_out, and_8_out, and_9_out, and_13_out, and_14_out, and_16_out, and_17_out, and_18_out,
       and_19_out, and_20_out, and_23_out, and_24_out, and_25_out, and_26_out, and_27_out, and_28_out,
       and_29_out, and_30_out, and_31_out, and_32_out, and_33_out, ANDop, AR_INR, AR_LD, B0, B1, B2, B3, B4,
       B5, B6, B7, B8, B9, B10, B11, CP, D0, D1, D2, D3, D4, D5, D6, D7, DR1, DR_0BIT, DR_INR, DR_LD, E_CLR,
       E_COMM, E_LD, EffOUT, I, IR_LD, MEMORY_WRITE_ENABLE, not_1_out, not_2_out, not_3_out, not_4_out,
       not_5_out, or_1_out, or_2_out, or_3_out, or_7_out, or_8_out, or_15_out, or_16_out, PC_INR, r, rB0,
       rB1, rB2, rB3, rB4, rB5, rB6, rB7, rB9, rB11, SC_CLR, SC_INR, T0, T2, T3, T4, T5, T6, T7;
  wire [2:0] ALU_SELECT, BUS_SELECT;

  not not_1 (not_1_out, D7);
  and and_1 (and_1_out, I, not_1_out, T3);
  and and_2 (AR_INR, D5, T4);
  Comparator #(.width(16)) comparator_1 (.a({16{1'b0}}), .b(ACOUT), .eq(AC_0BIT));  // open: gt, lt
  or or_1 (or_1_out, D0, D1, D2, D6);
  and and_3 (DR_INR, D6, T5);
  or or_2 (or_2_out, D0, D1, D2, D5);
  or or_3 (or_3_out, D3, D4);
  or or_4 (AR_LD, and_1_out, T2, T0);
  and and_4 (DR_LD, or_1_out, T4);
  and and_5 (and_5_out, or_2_out, T5);
  and and_6 (and_6_out, or_3_out, T4);
  and and_7 (and_7_out, D6, T6);
  and and_8 (and_8_out, D4, T4);
  and and_9 (and_9_out, D5, T5);
  Comparator #(.width(16)) comparator_2 (.a({16{1'b0}}), .b(DROUT), .eq(DR_0BIT));  // open: gt, lt
  or or_5 (SC_CLR, and_5_out, r, rB0, and_6_out, and_7_out);
  or or_6 (A1, and_8_out, and_9_out);
  and and_10 (ANDop, D0, T5);
  and and_11 (ADDop, D1, T5);
  and and_12 (DR1, D2, T5);
  control_unit control_unit_1 (
    .SC_INR(SC_INR), .SC_CLR(SC_CLR), .CLk(CP), .DECODEENABLE(1'b1), .IR_OUT(IROUT), .CONTROL(T2), .T0(T0),
    .T1(IR_LD), .T2(T2), .T3(T3), .T4(T4), .T5(T5), .T6(T6), .T7(T7), .rB0(rB0), .rB1(rB1), .rB2(rB2),
    .rB3(rB3), .rB4(rB4), .rB5(rB5), .rB6(rB6), .rB7(rB7), .rB8(E_COMM), .rB9(rB9), .rB10(E_CLR),
    .rB11(rB11), .r(r), .B0(B0), .B1(B1), .B2(B2), .B3(B3), .B4(B4), .B5(B5), .B6(B6), .B7(B7), .B8(B8),
    .B9(B9), .B10(B10), .B11(B11), .D0(D0), .D1(D1), .D2(D2), .D3(D3), .D4(D4), .D5(D5), .D6(D6), .D7(D7),
    .I(I));
  not not_2 (not_2_out, ACOUT[15]);
  not not_3 (not_3_out, EffOUT);
  and and_13 (and_13_out, D2, T5);
  and and_14 (and_14_out, D6, T6);
  and and_15 (A4, D3, T4);
  // Probe on ALU_SELECT
  Priority_Encoder priority_encoder_1 (
    .in1(ANDop), .in2(ADDop), .in3(DR1), .in5(rB9), .in6(rB7), .in7(rB6), .out(ALU_SELECT), .en_in(1'b1));  // open: in0, in4, gs, en_out
  and and_16 (and_16_out, rB3, ACOUT[15]);
  and and_17 (and_17_out, rB2, AC_0BIT);
  and and_18 (and_18_out, rB4, not_2_out);
  and and_19 (and_19_out, rB1, not_3_out);
  and and_20 (and_20_out, D6, T6);
  or or_7 (or_7_out, D0, D1, D2);
  or or_8 (or_8_out, B6, B7, B9);
  and and_21 (AC_INR, r, B5);
  and and_22 (AC_CLR, r, B11);
  or or_9 (A3, and_13_out, and_14_out);
  and and_23 (and_23_out, and_20_out, DR_0BIT);
  and and_24 (and_24_out, D1, T5);
  Priority_Encoder priority_encoder_2 (
    .in1(A1), .in2(A2), .in3(A3), .in4(A4), .in5(1'b0), .in6(A6), .in7(A7), .out(BUS_SELECT), .en_in(1'b1));  // open: in0, gs, en_out
  and and_25 (and_25_out, or_7_out, T5);
  and and_26 (and_26_out, or_8_out, r);
  or or_10 (E_LD, and_24_out, E_COMM, rB6, rB7);
  and and_27 (and_27_out, D5, T4);
  // Probe on BUS_SELECT
  or or_11 (PC_INR, IR_LD, and_16_out, and_17_out, and_18_out, and_19_out, and_23_out);
  or or_12 (AC_LD, and_25_out, and_26_out);
  or or_13 (A2, and_27_out, T0);
  or or_14 (A6, T2, 1'b0);
  Clock clock_1 (.out(CP));
  not not_4 (not_4_out, rB0);
  or or_15 (or_15_out, Start, and_28_out);
  and and_28 (and_28_out, not_4_out, SC_INR);
  or or_16 (or_16_out, D0, D1, D2, D6);
  not not_5 (not_5_out, D7);
  D_Flip_Flop d_ff_1 (.D(or_15_out), .clk(CP), .Q(SC_INR));  // open: Qn, preset, reset
  and and_29 (and_29_out, D3, T4);
  and and_30 (and_30_out, D5, T4);
  and and_31 (and_31_out, D6, T6);
  and and_32 (and_32_out, or_16_out, T4);
  and and_33 (and_33_out, not_5_out, I, T3);
  Data_path data_path_1 (
    .CLK(CP), .AR_INR(AR_INR), .BUS_SELECT(BUS_SELECT), .AR_LD(AR_LD), .PC_INR(PC_INR), .PC_LD(A1),
    .DR_INR(DR_INR), .DR_LD(DR_LD), .AC_INR(AC_INR), .AC_CLR(AC_CLR), .AC_LD(AC_LD), .ALU_SELECT(ALU_SELECT),
    .E_COMP(E_COMM), .E_CLR(E_CLR), .E_LD(E_LD), .IR_LD(IR_LD), .MEMORY_WRITE_ENABLE(MEMORY_WRITE_ENABLE),
    .MEMORY_OUT_ENABLE(A7), .rB6(rB6), .rB7(rB7), .ADD(ADDop), .DRout(DROUT), .ACout(ACOUT), .Eout(EffOUT),
    .IRout(IROUT));  // open: AR_CLR, PC_CLR, DR_CLR, Cin, PCout
  or or_17 (A7, and_32_out, and_33_out, IR_LD);
  or or_18 (MEMORY_WRITE_ENABLE, and_29_out, and_30_out, and_31_out);

  // Other names for the same wires on the sheet: AC_15BIT = ACOUT[15]; PC_LD = A1; rB8 = E_COMM; rB10 = E_CLR;
  //   T1 = IR_LD

  // Notes on the sheet:
  //   MATRIX CPU
endmodule
